// Logisim project 201811970CGB2.circ as structural Verilog: 1 circuit, main circuit main
module main (
  input  x,
  input  y,
  output S
);

  wire and_1_out, and_2_out, clock_1_out, d_ff_1_q, or_1_out, xor_1_out;

  Clock clock_1 (.out(clock_1_out));
  and and_1 (and_1_out, x, y);
  xor xor_1 (xor_1_out, x, y);
  D_Flip_Flop d_ff_1 (.clk(clock_1_out), .D(or_1_out), .Q(d_ff_1_q));  // open: Qn, preset, en, reset
  and and_2 (and_2_out, xor_1_out, d_ff_1_q);
  xor xor_2 (S, xor_1_out, d_ff_1_q);
  or or_1 (or_1_out, and_2_out, and_1_out);
endmodule
